# Fritzing sketch Wekker (saved by Fritzing 0.7.12b)

parts:
  part = Arduino
  Grote_rode_knop = Round Pushbutton
  Settings = Round Pushbutton
  Draaiknop = Rotary Encoder [package=THT]
  Klok = Real Time Clock Module - DS1307 RTC Breakout Board
  Wekker_aan/uit = Tilt Switch [package=THT]
  Radio_aan/uit = Tilt Switch [package=THT]  # not connected
  Display = atmega328 [package=dip]
  U2 = mystery part, 5 pins [chip_label=KIT-10733]

nets:
  GND: part.GND, Grote_rode_knop.leg1, Settings.leg1, Draaiknop.EncoderPinC, Klok.GND, Wekker_aan/uit.Pin_2, Display.GND, U2.pin1
  N1: part.D10, Display.D0_(RX)
  N2: part.D8, Wekker_aan/uit.Pin_1
  N3: part.D6, Grote_rode_knop.leg0
  N4: part.D4, Settings.leg0
  N5: part.D2, U2.pin2
  +5V: part.+5V, Klok.5V, Display.VCC, U2.pin3
  N6: part.A0, Draaiknop.EncoderPinB
  N7: part.A1, Draaiknop.EncoderPinA
  N8: part.A4, Klok.SDA
  N9: part.A5, Klok.SCL
